# Fritzing sketch Circuit (saved by Fritzing 0.9.2b)
breadboards: 1

parts:
  3d_Scanner = Arduino Uno (Rev3)
  Pan_Servo = Basic Servo
  Sensor = Infrared Proximity Sensor
  Tilt_Servo = Basic Servo

nets:
  N1: 3d_Scanner.A0, Sensor.Vout
  N2: 3d_Scanner.D9_PWM, Tilt_Servo.pulse
  N3: 3d_Scanner.D10_PWM/SS, Pan_Servo.pulse
  GND: 3d_Scanner.GND, Pan_Servo.gnd, Sensor.GND, Tilt_Servo.gnd
  VCC: 3d_Scanner.5V, Pan_Servo.vcc, Sensor.Vcc, Tilt_Servo.vcc
